# Fritzing sketch Untitled Sketch 2 (saved by Fritzing 0.8.7b)

parts:
  Part1 = Arduino Mega 2560 (Rev3)
  L298N1 = L298N DC motor driver
  Motor1 = DC Motor
  M2 = DC Motor
  U1 = LIPO-2000mAh [package=lipo-2000]  # not connected
  U2 = LIPO-2000mAh [package=lipo-2000]  # not connected
  CONN1 = USB connector [package=THT]  # not connected
  S1 = Round Pushbutton
  U3 = V_REG_MIC5235 [package=sot23-5]
  M3 = DC Motor
  S2 = SWITCH-MOMENTARY-2 [package=tactile-switch-1101ne]  # not connected

nets:
  N1: Part1.GND, M3.pin_1
  N2: Part1.D13_PWM, M3.pin_2
  N3: Part1.D11_PWM, L298N1.ENA
  N4: Part1.D10_PWM, L298N1.IN1
  N5: Part1.D9_PWM, L298N1.IN2
  N6: Part1.D8_PWM, L298N1.IN3
  N7: Part1.D6_PWM, L298N1.ENB
  N8: Part1.D7_PWM, L298N1.IN4
  N9: L298N1.OUT1, M2.pin_2
  N10: L298N1.OUT2, M2.pin_1
  N11: L298N1.OUT3, Motor1.pin_2
  N12: L298N1.OUT4, Motor1.pin_1
  N13: S1.leg1, U3.IN

notes:
  NVIDIA TX2
  Voltage Regulator 12V
  voltage meter+alarm
  Water Pump
  USB Connection, communicate w/Serial
  Normal ON/OFF switch
  EMERGENCY STOP

custom parts:
  L298N DC motor driver: 2x DC motor driver with 78M05 positive voltage regulator (7..35 V) L298N: max 46 V, 2 A Set 5 V Enable jumper to enable 5 V regultor (needed for the L298N) and +5 V output at screw terminal or supply external +5 V at screw terminal Set ENA and/or ENB to +5 V to enable motor permanently or supply ENA and/or ENB with PWM signal IN1 and IN2 set rotation directory for motor A (OUT1/OUT2) IN2 and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
